# Fritzing sketch weatherStation_simple (saved by Fritzing 0.9.3b)
circuit board: 8.46667cm x 5.64444cm
perfboards: 1

parts:
  DHT1 = DHT11 Humitidy and Temperature Sensor
  U12 = NodeMCU V1.0
  R1 = Resistor [tolerance=±5% resistance=10k package="0402 [SMD]"]
  Componente1 = Barometric Pressure Sensor - BMP180 Breakout (GY-68)

nets:
  VDD: DHT1.VDD, R1.Pin_0, Componente1.VCC
  N1: DHT1.DATA, U12.D4, R1.Pin_1
  GND: DHT1.GND, U12.GND, Componente1.SDA
  N2: U12.D1, Componente1.SCL
  N3: U12.D2, Componente1.GND

custom parts:
  DHT11 Humitidy and Temperature Sensor: DHT11 Humidity and Temperature Sensor
  NodeMCU V1.0: ESP8266 based NodeMCU

// code stored in the sketch: ws_blynk.ino
/*************************************************************
  Download latest Blynk library here:
    https://github.com/blynkkk/blynk-library/releases/latest

  Blynk is a platform with iOS and Android apps to control
  Arduino, Raspberry Pi and the likes over the Internet.
  You can easily build graphic interfaces for all your
  projects by simply dragging and dropping widgets.

    Downloads, docs, tutorials: http://www.blynk.cc
    Sketch generator:           http://examples.blynk.cc
    Blynk community:            http://community.blynk.cc
    Follow us:                  http://www.fb.com/blynkapp
                                http://twitter.com/blynk_app

  Blynk library is licensed under MIT license
  This example code is in public domain.

 *************************************************************

  This example shows how value can be pushed from Arduino to
  the Blynk App.

  WARNING :
  For this example you'll need Adafruit DHT sensor libraries:
    https://github.com/adafruit/Adafruit_Sensor
    https://github.com/adafruit/DHT-sensor-library

  App project setup:
    Value Display widget attached to V5
    Value Display widget attached to V6
 *************************************************************/

/* Comment this out to disable prints and save space */
#define BLYNK_PRINT Serial


#include <ESP8266WiFi.h>
#include <BlynkSimpleEsp8266.h>
#include <DHT.h>

//library bmp180
#include <SFE_BMP180.h>
#include <Wire.h>
#include <Adafruit_Sensor.h>
#include <Adafruit_BMP085_U.h>

Adafruit_BMP085_Unified bmp = Adafruit_BMP085_Unified(10085);

// You should get Auth Token in the Blynk App.
// Go to the Project Settings (nut icon).
char auth[] = "eeeacdbbc23d4eae90159a24faed61c5";

// Your WiFi credentials.
// Set password to "" for open networks.
char ssid[] = "WebCube4-6511";  // "Avalon";
char pass[] = "JE66Y5Q6";       // "17a18948a969";

#define DHTPIN 2          // What digital pin we're connected to

// Uncomment whatever type you're using!
#define DHTTYPE DHT11     // DHT 11
//#define DHTTYPE DHT22   // DHT 22, AM2302, AM2321
//#define DHTTYPE DHT21   // DHT 21, AM2301

DHT dht(DHTPIN, DHTTYPE);
BlynkTimer timer;

// This function sends Arduino's up time every second to Virtual Pin (5).
// In the app, Widget's reading frequency should be set to PUSH. This means
// that you define how often to send data to Blynk App.
void sendSensor()
{
  
  //--------------------------DHT22/DHT11-------------------------

  float h = dht.readHumidity();
  float t = dht.readTemperature(); // or dht.readTemperature(true) for Fahrenheit

  if (isnan(h) || isnan(t)) {
    Serial.println("Failed to read from DHT sensor!");
    return;
  }

  double gamma = log(h/100) + ((17.62*t) / (243.5+t));
  double dp = 243.5*gamma / (17.62-gamma);

  //--------------------------BMP180------------------------
  
  if(!bmp.begin()) {
    Serial.print("Failed to read from BMP sensor!!");
    while(1);
  }
  
  sensors_event_t event;
  bmp.getEvent(&event);

  //--------------------------------------------------------
  
  // You can send any value at any time.
  // Please don't send more that 10 values per second.
  Blynk.virtualWrite(V5, h);
  Blynk.virtualWrite(V6, t);
  Blynk.virtualWrite(V7, dp);
  Blynk.virtualWrite(V8, event.pressure);
}

void setup()
{
  // Debug console
  Serial.begin(115200);

  Blynk.begin(auth, ssid, pass);
  // You can also specify server:
  //Blynk.begin(auth, ssid, pass, "blynk-cloud.com", 8442);
  //Blynk.begin(auth, ssid, pass, IPAddress(192,168,1,100), 8442);

  dht.begin();

  // Setup a function to be called every second
  timer.setInterval(1000L, sendSensor);
}

void loop()
{
  Blynk.run();
  timer.run();
}
